// Digital circuit Flip Flop D.dig as structural Verilog
module Flip_Flop_D (
  input  in_1,
  input  clk,
  output out_2,
  output out_3
);

  wire nand_1_out, nand_2_out, not_1_out;

  not not_1 (not_1_out, in_1);
  nand nand_1 (nand_1_out, in_1, clk);
  nand nand_2 (nand_2_out, not_1_out, clk);
  nand nand_3 (out_2, nand_1_out, out_3);
  nand nand_4 (out_3, out_2, nand_2_out);
endmodule
