// Digital circuit FlipFlop_JK.dig as structural Verilog
module FlipFlop_JK (
  input  J,
  input  K,
  input  clk,
  output out_3,
  output out_4
);

  wire nand_1_out, nand_2_out;

  nand nand_1 (nand_1_out, out_4, J, clk);
  nand nand_2 (nand_2_out, clk, K, out_3);
  nand nand_3 (out_3, nand_1_out, out_4);
  nand nand_4 (out_4, out_3, nand_2_out);

  // Notes on the sheet:
  //   J: default 1
endmodule
