// Digital circuit FlipFlop_T.dig as structural Verilog
module FlipFlop_T (
  input  _0,
  output out_1,
  output out_2
);

  wire button_1_out, nand_1_out, nand_2_out;

  Button button_1 (.out(button_1_out));
  nand nand_1 (nand_1_out, out_2, _0, button_1_out);
  nand nand_2 (nand_2_out, button_1_out, _0, out_1);
  nand nand_3 (out_1, nand_1_out, out_2);
  nand nand_4 (out_2, out_1, nand_2_out);
endmodule
