// Digital circuit Full Adder.dig as structural Verilog
module Full_Adder (
  input  A,
  input  B,
  input  C,
  output Q,
  output Y
);

  wire and_1_out, and_2_out, xor_1_out;

  xor xor_1 (xor_1_out, A, B);
  and and_1 (and_1_out, A, B);
  and and_2 (and_2_out, xor_1_out, C);
  xor xor_2 (Q, xor_1_out, C);
  or or_1 (Y, and_1_out, and_2_out);
endmodule
