// Digital circuit flip flop rs.dig as structural Verilog
module flip_flop_rs (
  input  A,
  input  B,
  input  ck,
  output Q,
  output Y
);

  wire and_1_out, and_2_out;

  and and_1 (and_1_out, A, ck);
  and and_2 (and_2_out, ck, B);
  nand nand_1 (Q, and_1_out, Y);
  nand nand_2 (Y, Q, and_2_out);
endmodule
