// Digital circuit clase.dig as structural Verilog
module clase (
  input  [3:0] A,
  input  [3:0] B,
  input  [3:0] C,
  input  [3:0] C_2,
  input  [3:0] in_6,
  input  [3:0] in_12,
  input  [3:0] clk,
  input  [3:0] in_14,
  output [3:0] carry,
  output [3:0] out_7,
  output [3:0] out_8,
  output [3:0] out_9,
  output [3:0] out_10,
  output [3:0] out_11,
  output [3:0] out_15,
  output [3:0] out_16,
  output [3:0] out_17,
  output [3:0] out_18
);

  wire [3:0] and_1_out, and_2_out, and_3_out, and_4_out, and_5_out, and_6_out, and_7_out, nand_1_out,
       nand_2_out, nand_3_out, nand_4_out, nand_5_out, nand_6_out, nand_7_out, nand_8_out, nand_9_out,
       nand_11_out, nand_13_out, nand_15_out, not_1_out, not_2_out, not_3_out, not_4_out, not_5_out,
       not_6_out, not_7_out, or_2_out, xor_1_out, xor_2_out, xor_3_out, xor_4_out;
  wire [3:1] undriven, undriven_2, undriven_3, undriven_4;

  assign xor_1_out = A ^ B;  // XOr xor_1, 4 bits wide
  assign xor_2_out = A ^ B;  // XOr xor_2, 4 bits wide
  assign not_1_out = ~A;  // Not not_1, 4 bits wide
  assign and_1_out = A & B;  // And and_1, 4 bits wide
  assign and_2_out = xor_1_out & C;  // And and_2, 4 bits wide
  assign and_3_out = B & not_1_out;  // And and_3, 4 bits wide
  assign xor_3_out = xor_1_out ^ C;  // XOr xor_3, 4 bits wide
  assign not_2_out = ~xor_2_out;  // Not not_2, 4 bits wide
  assign xor_4_out = in_6 ^ xor_2_out;  // XOr xor_4, 4 bits wide
  assign and_4_out = not_2_out & in_6;  // And and_4, 4 bits wide
  assign carry = and_1_out | and_2_out;  // Or or_1, 4 bits wide
  assign out_7 = and_4_out ^ and_3_out;  // XOr xor_5, 4 bits wide
  assign not_3_out = ~C_2;  // Not not_3, 4 bits wide
  assign and_5_out = xor_3_out & not_3_out;  // And and_5, 4 bits wide
  assign and_6_out = xor_4_out & C_2;  // And and_6, 4 bits wide
  assign or_2_out = and_5_out | and_6_out;  // Or or_2, 4 bits wide
  assign and_7_out = in_12 & clk;  // And and_7, 4 bits wide
  assign not_4_out = ~{undriven_3, or_2_out[3]};  // Not not_4, 4 bits wide
  assign not_5_out = ~{undriven_4, or_2_out[2]};  // Not not_5, 4 bits wide
  assign not_6_out = ~{undriven, or_2_out[1]};  // Not not_6, 4 bits wide
  assign not_7_out = ~{undriven_2, or_2_out[0]};  // Not not_7, 4 bits wide
  assign nand_1_out = ~({undriven_3, or_2_out[3]} & and_7_out);  // NAnd nand_1, 4 bits wide
  assign nand_2_out = ~(not_4_out & and_7_out);  // NAnd nand_2, 4 bits wide
  assign nand_3_out = ~({undriven_4, or_2_out[2]} & and_7_out);  // NAnd nand_3, 4 bits wide
  assign nand_4_out = ~(not_5_out & and_7_out);  // NAnd nand_4, 4 bits wide
  assign nand_5_out = ~({undriven, or_2_out[1]} & and_7_out);  // NAnd nand_5, 4 bits wide
  assign nand_6_out = ~(not_6_out & and_7_out);  // NAnd nand_6, 4 bits wide
  assign nand_7_out = ~({undriven_2, or_2_out[0]} & and_7_out);  // NAnd nand_7, 4 bits wide
  assign nand_8_out = ~(not_7_out & and_7_out);  // NAnd nand_8, 4 bits wide
  assign nand_9_out = ~(nand_1_out & out_8);  // NAnd nand_9, 4 bits wide
  assign out_8 = ~(nand_9_out & nand_2_out);  // NAnd nand_10, 4 bits wide
  assign nand_11_out = ~(nand_3_out & out_9);  // NAnd nand_11, 4 bits wide
  assign out_9 = ~(nand_11_out & nand_4_out);  // NAnd nand_12, 4 bits wide
  assign nand_13_out = ~(nand_5_out & out_10);  // NAnd nand_13, 4 bits wide
  assign out_10 = ~(nand_13_out & nand_6_out);  // NAnd nand_14, 4 bits wide
  assign nand_15_out = ~(nand_7_out & out_11);  // NAnd nand_15, 4 bits wide
  assign out_11 = ~(nand_15_out & nand_8_out);  // NAnd nand_16, 4 bits wide
  Multiplexer #(.Bits(4)) multiplexer_1 (
    .sel(in_14[0]), .in_0(4'b0000), .in_1(nand_9_out), .out({out_15[0], out_16[0], out_17[0], out_18[0]}));
  // Pins of 1 and 4 bits meet at {undriven_3, or_2_out[3]}
  // Pins of 1 and 4 bits meet at {undriven_4, or_2_out[2]}
  // Pins of 1 and 4 bits meet at nand_11_out
  // Pins of 1 and 4 bits meet at {undriven, or_2_out[1]}
  // Pins of 1 and 4 bits meet at nand_13_out
  // Pins of 1 and 4 bits meet at {undriven_2, or_2_out[0]}
  // Pins of 1 and 4 bits meet at nand_15_out
  // Pins of 1 and 4 bits meet at clk
  // Pins of 1 and 4 bits meet at in_14
  // Pins of 1 and 4 bits meet at out_18
  // Pins of 1 and 4 bits meet at out_17
  // Pins of 1 and 4 bits meet at out_16

  // Notes on the sheet:
  //   sumador 4bits
  //   restador 4 bits
  //   mux 2 a 1 de 4 bits
  //   flipflop D
endmodule
