// Digital circuit restadorCompleto.dig as structural Verilog
module restadorCompleto (
  input  [3:0] in_1,
  input  [3:0] in_2,
  input  [3:0] in_3,
  output [3:0] out_4,
  output [3:0] out_5
);

  wire [3:0] and_1_out, and_2_out, not_1_out, not_2_out, xor_1_out;

  assign xor_1_out = in_1 ^ in_2;  // XOr xor_1, 4 bits wide
  assign not_1_out = ~in_1;  // Not not_1, 4 bits wide
  assign and_1_out = in_2 & not_1_out;  // And and_1, 4 bits wide
  assign not_2_out = ~xor_1_out;  // Not not_2, 4 bits wide
  assign out_4 = in_3 ^ xor_1_out;  // XOr xor_2, 4 bits wide
  assign and_2_out = not_2_out & in_3;  // And and_2, 4 bits wide
  assign out_5 = and_2_out ^ and_1_out;  // XOr xor_3, 4 bits wide

  // Notes on the sheet:
  //   full subtractor
endmodule
