// Digital circuit Demux.dig as structural Verilog
module Demux (
  input  [15:0] Selector,
  input  [15:0] Q,
  output s0,
  output s1,
  output s2,
  output s3,
  output s4,
  output s5,
  output s6,
  output s7,
  output s8,
  output s9,
  output s10,
  output s11,
  output s12,
  output s13,
  output s14,
  output s15
);

  wire not_1_out, not_2_out, not_3_out, not_4_out;

  not not_1 (not_1_out, Selector[3]);
  not not_2 (not_2_out, Selector[2]);
  not not_3 (not_3_out, Selector[1]);
  not not_4 (not_4_out, Selector[0]);
  and and_1 (s0, not_1_out, not_2_out, not_3_out, not_4_out, Q[0]);
  and and_2 (s1, not_1_out, not_2_out, not_3_out, Selector[0], Q[1]);
  and and_3 (s2, not_1_out, not_2_out, Selector[1], not_4_out, Q[2]);
  and and_4 (s3, not_1_out, not_2_out, Selector[1], Selector[0], Q[3]);
  and and_5 (s4, not_1_out, Selector[2], not_3_out, not_4_out, Q[4]);
  and and_6 (s5, not_1_out, Selector[2], not_3_out, Selector[0], Q[5]);
  and and_7 (s6, not_1_out, Selector[2], Selector[1], not_4_out, Q[6]);
  and and_8 (s7, not_1_out, Selector[2], Selector[1], Selector[0], Q[7]);
  and and_9 (s8, Selector[3], not_2_out, not_3_out, not_4_out, Q[8]);
  and and_10 (s9, Selector[3], not_2_out, not_3_out, Selector[0], Q[9]);
  and and_11 (s10, Selector[3], not_2_out, Selector[1], not_4_out, Q[10]);
  and and_12 (s11, Selector[3], not_2_out, Selector[1], Selector[0], Q[11]);
  and and_13 (s12, Selector[3], Selector[2], not_3_out, not_4_out, Q[12]);
  and and_14 (s13, Selector[3], Selector[2], not_3_out, Selector[0], Q[13]);
  and and_15 (s14, Selector[3], Selector[2], Selector[1], not_4_out, Q[14]);
  and and_16 (s15, Selector[3], Selector[2], Selector[1], Selector[0], Q[15]);

  // Notes on the sheet:
  //   Selector: Bit 1 of the input selection.
  //   {{de Bit 1 der Signalauswahl.}}
endmodule
