// Digital circuit Mux.dig as structural Verilog
module Mux (
  input  [3:0] D_0,
  input  [3:0] D_1,
  input  [3:0] D_2,
  input  [3:0] D_3,
  input  [3:0] D_4,
  input  [3:0] D_5,
  input  [3:0] D_6,
  input  [3:0] D_7,
  input  [3:0] D_8,
  input  [3:0] D_9,
  input  [3:0] D_10,
  input  [3:0] D_11,
  input  [3:0] D_12,
  input  [3:0] D_13,
  input  [3:0] D_14,
  input  [3:0] D_15,
  input  [15:0] Sel,
  output [3:0] s
);

  wire [3:0] and_1_out, and_2_out, and_3_out, and_4_out, and_5_out, and_6_out, and_7_out, and_8_out,
       and_9_out, and_10_out, and_11_out, and_12_out, and_13_out, and_14_out, and_15_out, and_16_out,
       not_1_out, not_2_out, not_3_out, not_4_out;

  assign not_1_out = ~Sel[15:12];  // Not not_1, 4 bits wide
  assign not_2_out = ~Sel[11:8];  // Not not_2, 4 bits wide
  assign not_3_out = ~Sel[7:4];  // Not not_3, 4 bits wide
  assign not_4_out = ~Sel[3:0];  // Not not_4, 4 bits wide
  assign and_1_out = not_1_out & not_2_out & not_3_out & not_4_out & D_0;  // And and_1, 4 bits wide
  assign and_2_out = not_1_out & not_2_out & not_3_out & Sel[3:0] & D_1;  // And and_2, 4 bits wide
  assign and_3_out = not_1_out & not_2_out & Sel[7:4] & not_4_out & D_2;  // And and_3, 4 bits wide
  assign and_4_out = not_1_out & not_2_out & Sel[7:4] & Sel[3:0] & D_3;  // And and_4, 4 bits wide
  assign and_5_out = not_1_out & Sel[11:8] & not_3_out & not_4_out & D_4;  // And and_5, 4 bits wide
  assign and_6_out = not_1_out & Sel[11:8] & not_3_out & Sel[3:0] & D_5;  // And and_6, 4 bits wide
  assign and_7_out = not_1_out & Sel[11:8] & Sel[7:4] & not_4_out & D_6;  // And and_7, 4 bits wide
  assign and_8_out = not_1_out & Sel[11:8] & Sel[7:4] & Sel[3:0] & D_7;  // And and_8, 4 bits wide
  assign and_9_out = Sel[15:12] & not_2_out & not_3_out & not_4_out & D_8;  // And and_9, 4 bits wide
  assign and_10_out = Sel[15:12] & not_2_out & not_3_out & Sel[3:0] & D_9;  // And and_10, 4 bits wide
  assign and_11_out = Sel[15:12] & not_2_out & Sel[7:4] & not_4_out & D_10;  // And and_11, 4 bits wide
  assign and_12_out = Sel[15:12] & not_2_out & Sel[7:4] & Sel[3:0] & D_11;  // And and_12, 4 bits wide
  assign and_13_out = Sel[15:12] & Sel[11:8] & not_3_out & not_4_out & D_12;  // And and_13, 4 bits wide
  assign and_14_out = Sel[15:12] & Sel[11:8] & not_3_out & Sel[3:0] & D_13;  // And and_14, 4 bits wide
  assign and_15_out = Sel[15:12] & Sel[11:8] & Sel[7:4] & not_4_out & D_14;  // And and_15, 4 bits wide
  assign and_16_out = Sel[15:12] & Sel[11:8] & Sel[7:4] & Sel[3:0] & D_15;  // And and_16, 4 bits wide
  assign s = and_1_out | and_2_out | and_3_out | and_4_out | and_5_out | and_6_out | and_7_out | and_8_out | and_9_out | and_10_out | and_11_out | and_12_out | and_13_out | and_14_out | and_15_out | and_16_out;  // Or or_1, 4 bits wide

  // Notes on the sheet:
  //   D_0: data bit 0.
  //   {{de Das 0. Datenbit.}}
  //   D_1: data bit 1.
  //   {{de Das 1. Datenbit.}}
  //   D_2: data bit 2.
  //   {{de Das 2. Datenbit.}}
  //   D_3: data bit 3.
  //   {{de Das 3. Datenbit.}}
  //   D_4: data bit 0.
  //   {{de Das 0. Datenbit.}}
  //   D_5: data bit 1.
  //   {{de Das 1. Datenbit.}}
  //   D_6: data bit 2.
  //   {{de Das 2. Datenbit.}}
  //   D_7: data bit 3.
  //   {{de Das 3. Datenbit.}}
  //   D_8: data bit 0.
  //   {{de Das 0. Datenbit.}}
  //   D_9: data bit 1.
  //   {{de Das 1. Datenbit.}}
  //   D_10: data bit 2.
  //   {{de Das 2. Datenbit.}}
  //   D_11: data bit 3.
  //   {{de Das 3. Datenbit.}}
  //   D_12: data bit 0.
  //   {{de Das 0. Datenbit.}}
  //   D_13: data bit 1.
  //   {{de Das 1. Datenbit.}}
  //   D_14: data bit 2.
  //   {{de Das 2. Datenbit.}}
  //   D_15: data bit 3.
  //   {{de Das 3. Datenbit.}}
  //   Sel: Bit 1 of the input selection.
  //   {{de Bit 1 der Signalauswahl.}}
endmodule
