// Digital circuit entrega3.dig as structural Verilog
module entrega3 (
  input  [3:0] A,
  input  [3:0] B,
  input  [3:0] C,
  input  [3:0] C_2,
  input  [3:0] in_6,
  input  write,
  input  [15:0] Dir,
  input  enable,
  input  clk,
  output [3:0] carry,
  output [3:0] out_7,
  output [3:0] Dout
);

  wire and_7_out, demux_1_s0, demux_1_s1, demux_1_s2, demux_1_s3, demux_1_s4, demux_1_s5, demux_1_s6,
       demux_1_s7, demux_1_s8, demux_1_s9, demux_1_s10, demux_1_s11, demux_1_s12, demux_1_s13, demux_1_s14,
       demux_1_s15;
  wire [3:0] and_1_out, and_2_out, and_3_out, and_4_out, and_5_out, and_6_out, mux_1_s, not_1_out, not_2_out,
       not_3_out, or_2_out, register_1_q, register_2_q, register_3_q, register_4_q, register_5_q,
       register_6_q, register_7_q, register_8_q, register_9_q, register_10_q, register_11_q, register_12_q,
       register_13_q, register_14_q, register_15_q, register_16_q, xor_1_out, xor_2_out, xor_3_out, xor_4_out;

  assign xor_1_out = A ^ B;  // XOr xor_1, 4 bits wide
  assign xor_2_out = A ^ B;  // XOr xor_2, 4 bits wide
  assign not_1_out = ~A;  // Not not_1, 4 bits wide
  assign and_1_out = A & B;  // And and_1, 4 bits wide
  assign and_2_out = xor_1_out & C;  // And and_2, 4 bits wide
  assign and_3_out = B & not_1_out;  // And and_3, 4 bits wide
  assign xor_3_out = xor_1_out ^ C;  // XOr xor_3, 4 bits wide
  assign not_2_out = ~xor_2_out;  // Not not_2, 4 bits wide
  assign xor_4_out = in_6 ^ xor_2_out;  // XOr xor_4, 4 bits wide
  assign and_4_out = not_2_out & in_6;  // And and_4, 4 bits wide
  assign carry = and_1_out | and_2_out;  // Or or_1, 4 bits wide
  assign out_7 = and_4_out ^ and_3_out;  // XOr xor_5, 4 bits wide
  assign not_3_out = ~C_2;  // Not not_3, 4 bits wide
  assign and_5_out = xor_3_out & not_3_out;  // And and_5, 4 bits wide
  assign and_6_out = xor_4_out & C_2;  // And and_6, 4 bits wide
  assign or_2_out = and_5_out | and_6_out;  // Or or_2, 4 bits wide
  and and_7 (and_7_out, clk, write);
  Demux demux_1 (
    .Selector(Dir), .Q({16{1'b0}}), .s0(demux_1_s0), .s1(demux_1_s1), .s2(demux_1_s2), .s3(demux_1_s3),
    .s4(demux_1_s4), .s5(demux_1_s5), .s6(demux_1_s6), .s7(demux_1_s7), .s8(demux_1_s8), .s9(demux_1_s9),
    .s10(demux_1_s10), .s11(demux_1_s11), .s12(demux_1_s12), .s13(demux_1_s13), .s14(demux_1_s14),
    .s15(demux_1_s15));
  Register #(.Bits(4)) register_1 (.D(or_2_out), .C(and_7_out), .en(demux_1_s0), .Q(register_1_q));
  Register #(.Bits(4)) register_2 (.D(or_2_out), .C(and_7_out), .en(demux_1_s1), .Q(register_2_q));
  Register #(.Bits(4)) register_3 (.D(or_2_out), .C(and_7_out), .en(demux_1_s2), .Q(register_3_q));
  Register #(.Bits(4)) register_4 (.D(or_2_out), .C(and_7_out), .en(demux_1_s3), .Q(register_4_q));
  Register #(.Bits(4)) register_5 (.D(or_2_out), .C(and_7_out), .en(demux_1_s4), .Q(register_5_q));
  Register #(.Bits(4)) register_6 (.D(or_2_out), .C(and_7_out), .en(demux_1_s5), .Q(register_6_q));
  Register #(.Bits(4)) register_7 (.D(or_2_out), .C(and_7_out), .en(demux_1_s6), .Q(register_7_q));
  Register #(.Bits(4)) register_8 (.D(or_2_out), .C(and_7_out), .en(demux_1_s7), .Q(register_8_q));
  Register #(.Bits(4)) register_9 (.D(or_2_out), .C(and_7_out), .en(demux_1_s8), .Q(register_9_q));
  Register #(.Bits(4)) register_10 (.D(or_2_out), .C(and_7_out), .en(demux_1_s9), .Q(register_10_q));
  Register #(.Bits(4)) register_11 (.D(or_2_out), .C(and_7_out), .en(demux_1_s10), .Q(register_11_q));
  Register #(.Bits(4)) register_12 (.D(or_2_out), .C(and_7_out), .en(demux_1_s11), .Q(register_12_q));
  Register #(.Bits(4)) register_13 (.D(or_2_out), .C(and_7_out), .en(demux_1_s12), .Q(register_13_q));
  Register #(.Bits(4)) register_14 (.D(or_2_out), .C(and_7_out), .en(demux_1_s13), .Q(register_14_q));
  Register #(.Bits(4)) register_15 (.D(or_2_out), .C(and_7_out), .en(demux_1_s14), .Q(register_15_q));
  Register #(.Bits(4)) register_16 (.D(or_2_out), .C(and_7_out), .en(demux_1_s15), .Q(register_16_q));
  Mux mux_1 (
    .D_0(register_1_q), .D_1(register_2_q), .D_2(register_3_q), .D_3(register_4_q), .D_4(register_5_q),
    .D_5(register_6_q), .D_6(register_7_q), .D_7(register_8_q), .D_8(register_9_q), .D_9(register_10_q),
    .D_10(register_11_q), .D_11(register_12_q), .D_12(register_13_q), .D_13(register_14_q),
    .D_14(register_15_q), .D_15(register_16_q), .Sel(Dir), .s(mux_1_s));
  D_FF #(.Bits(4)) d_ff_1 (.D(mux_1_s), .C(enable), .Q(Dout));  // open: nQ

  // Notes on the sheet:
  //   sumador 4bits
  //   restador 4 bits
  //   mux 2 a 1 de 4 bits
  //   memory
endmodule
