// Digital circuit full adder 4 bits.dig as structural Verilog
module full_adder_4_bits (
  input  [3:0] A,
  input  [3:0] B,
  input  [3:0] C,
  output [3:0] Q,
  output [3:0] Y
);

  wire [3:0] and_1_out, and_2_out, xor_1_out;

  assign xor_1_out = A ^ B;  // XOr xor_1, 4 bits wide
  assign and_1_out = A & B;  // And and_1, 4 bits wide
  assign and_2_out = xor_1_out & C;  // And and_2, 4 bits wide
  assign Q = xor_1_out ^ C;  // XOr xor_2, 4 bits wide
  assign Y = and_1_out | and_2_out;  // Or or_1, 4 bits wide
endmodule
