// Digital circuit memory.dig as structural Verilog
module memory (
  input  D_in,
  input  clock,
  input  write,
  input  [2:0] Dir,
  input  enable,
  output Dout
);

  wire and_1_out, demultiplexer_1_out_0, demultiplexer_1_out_1, demultiplexer_1_out_2, demultiplexer_1_out_3,
       demultiplexer_1_out_4, demultiplexer_1_out_5, demultiplexer_1_out_6, demultiplexer_1_out_7,
       multiplexer_1_out, register_1_q, register_2_q, register_3_q, register_4_q, register_5_q, register_6_q,
       register_7_q, register_8_q;

  and and_1 (and_1_out, clock, write);
  Demultiplexer #(.Selector_Bits(3)) demultiplexer_1 (
    .sel(Dir), .in(1'b1), .out_0(demultiplexer_1_out_0), .out_1(demultiplexer_1_out_1),
    .out_2(demultiplexer_1_out_2), .out_3(demultiplexer_1_out_3), .out_4(demultiplexer_1_out_4),
    .out_5(demultiplexer_1_out_5), .out_6(demultiplexer_1_out_6), .out_7(demultiplexer_1_out_7));
  Register register_1 (.D(D_in), .C(and_1_out), .en(demultiplexer_1_out_0), .Q(register_1_q));
  Register register_2 (.D(D_in), .C(and_1_out), .en(demultiplexer_1_out_1), .Q(register_2_q));
  Register register_3 (.D(D_in), .C(and_1_out), .en(demultiplexer_1_out_2), .Q(register_3_q));
  Register register_4 (.D(D_in), .C(and_1_out), .en(demultiplexer_1_out_3), .Q(register_4_q));
  Register register_5 (.D(D_in), .C(and_1_out), .en(demultiplexer_1_out_4), .Q(register_5_q));
  Register register_6 (.D(D_in), .C(and_1_out), .en(demultiplexer_1_out_5), .Q(register_6_q));
  Register register_7 (.D(D_in), .C(and_1_out), .en(demultiplexer_1_out_6), .Q(register_7_q));
  Register register_8 (.D(D_in), .C(and_1_out), .en(demultiplexer_1_out_7), .Q(register_8_q));
  Multiplexer #(.Selector_Bits(3)) multiplexer_1 (
    .sel(Dir), .in_0(register_1_q), .in_1(register_2_q), .in_2(register_3_q), .in_3(register_4_q),
    .in_4(register_5_q), .in_5(register_6_q), .in_6(register_7_q), .in_7(register_8_q),
    .out(multiplexer_1_out));
  D_FF d_ff_1 (.D(multiplexer_1_out), .C(enable), .Q(Dout));  // open: nQ
endmodule
