// Digital circuit mux2a1.dig as structural Verilog
module mux2a1 (
  input  in_2,
  input  in_3,
  input  in_4,
  output out_1
);

  wire and_1_out, and_2_out, not_1_out;

  not not_1 (not_1_out, in_4);
  and and_1 (and_1_out, in_2, not_1_out);
  and and_2 (and_2_out, in_3, in_4);
  or or_1 (out_1, and_1_out, and_2_out);

  // Notes on the sheet:
  //   mux
endmodule
