// Digital circuit progam counter.dig as structural Verilog
module progam_counter (
  input  reset,
  input  wen,
  input  clock,
  output [4:0] Output,
  output ovf
);

  Counter #(.Bits(5)) counter_1 (.en(wen), .C(clock), .clr(reset), .out(Output), .ovf(ovf));

  // Notes on the sheet:
  //   Output: El contador de programa actual
  //   reset: Provoca un salto absoluto. El valor de la entrada de la ALU se utiliza como la nueva dirección
  //   wen: Se activa si hay un salto relativo. El valor de la entrada de la ALU se le suma a la dirección actual
  //   ovf: El contador de programa actual
endmodule
