// Digital circuit ALU.dig as structural Verilog
module ALU (
  input  [3:0] ALUOp,
  input  in_3,
  input  [31:0] A,
  input  in_5,
  input  [31:0] B,
  output [31:0] out
);

  wire slt_lt, sltu_lt;
  wire [31:0] add, \and , div, mul, \or , sll, slt, sltu, sra, srl, sub, \xor ;
  wire [63:32] mul_1_mul;

  Add #(.Bits(32)) add_1 (.a(A), .b(B), .c_i(1'b0), .s(add));  // open: c_o
  Sub #(.Bits(32)) sub_1 (.a(A), .b(B), .c_i(1'b0), .s(sub));  // open: c_o
  assign \xor  = A ^ B;  // XOr xor_1, 32 bits wide
  assign \or  = A | B;  // Or or_1, 32 bits wide
  assign \and  = A & B;  // And and_1, 32 bits wide
  Mul #(.Bits(32)) mul_1 (.a(A), .b(B), .mul({mul_1_mul, mul}));
  Div #(.Bits(32)) div_1 (.a(A), .b(B), .q(div));  // open: r
  BarrelShifter #(.Bits(32)) u_sll (.in(A), .shift(B[5:0]), .out(sll));
  BarrelShifter #(.Bits(32), .direction("right")) u_srl (.in(A), .shift(B[5:0]), .out(srl));
  BarrelShifter #(.barrelShifterMode("arithmetic"), .Bits(32), .direction("right")) u_sra (
    .in(A), .shift(B[5:0]), .out(sra));
  Comparator #(.Signed("true"), .Bits(32)) u_slt (.a(A), .b(B), .lt(slt_lt));  // open: gt, eq
  Comparator #(.Bits(32)) u_sltu (.a(A), .b(B), .lt(sltu_lt));  // open: gt, eq
  BitExtender #(.inputBits(1), .outputBits(32)) bitextender_1 (.in(slt_lt), .out(slt));
  BitExtender #(.inputBits(1), .outputBits(32)) bitextender_2 (.in(sltu_lt), .out(sltu));
  Multiplexer #(.Selector_Bits(4), .Bits(32)) multiplexer_1 (
    .sel(ALUOp), .in_0(add), .in_1(sll), .in_2(slt), .in_3(sltu), .in_4(\xor ), .in_5(srl), .in_6(\or ),
    .in_7(\and ), .in_8(sub), .in_9({32{1'b0}}), .in_10({32{1'b0}}), .in_11({32{1'b0}}), .in_12({32{1'b0}}),
    .in_13(sra), .in_14(mul), .in_15(div), .out(out));
  // Pins of 1 and 32 bits meet at A
  // Pins of 1 and 32 bits meet at B
endmodule
