// Digital circuit ALU_nBits.dig as structural Verilog
module ALU_nBits (
  input  [2:0] f3,
  input  [31:0] op_1,
  input  [31:0] op_2,
  output [31:0] out
);

  wire [31:0] add, \and , div, mul, notconnected_1_out, \or , sub, \xor ;
  wire [63:32] mul_1_mul;

  Add #(.Bits(32)) add_1 (.a(op_1), .b(op_2), .c_i(1'b0), .s(add));  // open: c_o
  Sub #(.Bits(32)) sub_1 (.a(op_1), .b(op_2), .c_i(1'b0), .s(sub));  // open: c_o
  assign \and  = op_1 & op_2;  // And and_1, 32 bits wide
  assign \or  = op_1 | op_2;  // Or or_1, 32 bits wide
  assign \xor  = op_1 ^ op_2;  // XOr xor_1, 32 bits wide
  Mul #(.Bits(32)) mul_1 (.a(op_1), .b(op_2), .mul({mul_1_mul, mul}));
  Div #(.Bits(32)) div_1 (.a(op_1), .b(op_2), .q(div));  // open: r
  Multiplexer #(.Selector_Bits(3), .Bits(32)) multiplexer_1 (
    .sel(f3), .in_0(add), .in_1(sub), .in_2(\and ), .in_3(\or ), .in_4(\xor ), .in_5(mul), .in_6(div),
    .in_7(notconnected_1_out), .out(out));
  // NotConnected on notconnected_1_out
endmodule
