// Digital circuit ControlUnit.dig as structural Verilog
// Cerebro del sistema. Establece las señales que toman decisiones dependiendo del tipo de instrucción y de operación
module ControlUnit (
  input  [6:0] Opcode,
  input  [2:0] Funct3,
  input  [6:0] Funct7,
  input  [4:0] Rd,
  output RUWr,
  output [2:0] ImmSrc,
  output ALUASrc,
  output ALUBSrc,
  output DMWr,
  output [4:0] BrOp,
  output [2:0] DMCtrl,
  output [3:0] ALUOp,
  output [1:0] RUDataWrSrc
);

  wire add, addi, addO, \and , and_8_out, and_9_out, and_10_out, and_11_out, and_12_out, and_20_out,
       and_21_out, and_22_out, andi, B, Br1, Br2, Br3, Br4, Br5, Br6, comparator_5_eq, comparator_6_eq,
       comparator_7_eq, comparator_8_eq, comparator_9_eq, comparator_10_eq, comparator_11_eq,
       comparator_12_eq, comparator_13_eq, comparator_14_eq, comparator_15_eq, comparator_16_eq, DMCtrl_3_eq,
       DMCtrl_eq, F7A, F7B, F7C, I, IL, IS, J, mul, mulO, \or , or_2_out, ori, R, Rd_t, S, sll, slli, slt,
       slti, sltiu, sltu, sra, srai, sraiO, sraO, srl, srli, srliO, srlO, sub, subO, U, \xor , xori;
  wire [2:0] DM, F3A, F3B;
  wire [3:0] Iop, Rop, Uop;
  wire [4:0] Br, BrB;
  wire [8:8] lookuptable_1_out;

  Comparator #(.Bits(5)) comparator_1 (.a(Rd), .b({5{1'b0}}), .eq(Rd_t));  // open: gt, lt
  Comparator #(.Bits(7)) Tipo_R (.a(Opcode), .b(7'b0110011), .eq(R));  // open: gt, lt
  Comparator #(.Bits(7)) Tipo_I (.a(Opcode), .b(7'b0010011), .eq(I));  // open: gt, lt
  Comparator #(.Bits(7)) Tipo_I_lectura (.a(Opcode), .b(7'b0000011), .eq(IL));  // open: gt, lt
  Comparator #(.Bits(7)) Tipo_S (.a(Opcode), .b(7'b0100011), .eq(S));  // open: gt, lt
  Comparator #(.Bits(7)) Tipo_B (.a(Opcode), .b(7'b1100011), .eq(B));  // open: gt, lt
  Comparator #(.Bits(7)) Tipo_I_salto (.a(Opcode), .b(7'b1100111), .eq(IS));  // open: gt, lt
  Comparator #(.Bits(7)) Tipo_J (.a(Opcode), .b(7'b1101111), .eq(J));  // open: gt, lt
  Comparator #(.Bits(7)) Tipo_U (.a(Opcode), .b(7'b0110111), .eq(U));  // open: gt, lt
  Comparator #(.Bits(3)) u_ADD (.a(Funct3), .b(3'b000), .eq(add));  // open: gt, lt
  Comparator #(.Bits(3)) u_SUB (.a(Funct3), .b(3'b000), .eq(sub));  // open: gt, lt
  Comparator #(.Bits(3)) u_SLL (.a(Funct3), .b(3'b001), .eq(sll));  // open: gt, lt
  Comparator #(.Bits(3)) u_SLT (.a(Funct3), .b(3'b010), .eq(slt));  // open: gt, lt
  Comparator #(.Bits(3)) u_SLTU (.a(Funct3), .b(3'b011), .eq(sltu));  // open: gt, lt
  Comparator #(.Bits(3)) u_XOR (.a(Funct3), .b(3'b100), .eq(\xor ));  // open: gt, lt
  Comparator #(.Bits(3)) u_SRL (.a(Funct3), .b(3'b101), .eq(srl));  // open: gt, lt
  Comparator #(.Bits(3)) u_SRA (.a(Funct3), .b(3'b101), .eq(sra));  // open: gt, lt
  Comparator #(.Bits(3)) u_OR (.a(Funct3), .b(3'b110), .eq(\or ));  // open: gt, lt
  Comparator #(.Bits(3)) u_AND (.a(Funct3), .b(3'b111), .eq(\and ));  // open: gt, lt
  Comparator #(.Bits(7)) comparator_2 (.a(Funct7), .b({7{1'b0}}), .eq(F7A));  // open: gt, lt
  Comparator #(.Bits(7)) comparator_3 (.a(Funct7), .b(7'b0100000), .eq(F7B));  // open: gt, lt
  Comparator #(.Bits(7)) comparator_4 (.a(Funct7), .b(7'b0000001), .eq(F7C));  // open: gt, lt
  Comparator #(.Bits(3)) comparator_5 (.a(Funct3), .b(3'b000), .eq(comparator_5_eq));  // open: gt, lt
  Comparator #(.Bits(3)) comparator_6 (.a(Funct3), .b(3'b001), .eq(comparator_6_eq));  // open: gt, lt
  Comparator #(.Bits(3)) comparator_7 (.a(Funct3), .b(3'b100), .eq(comparator_7_eq));  // open: gt, lt
  Comparator #(.Bits(3)) comparator_8 (.a(Funct3), .b(3'b101), .eq(comparator_8_eq));  // open: gt, lt
  Comparator #(.Bits(3)) comparator_9 (.a(Funct3), .b(3'b110), .eq(comparator_9_eq));  // open: gt, lt
  Comparator #(.Bits(3)) comparator_10 (.a(Funct3), .b(3'b111), .eq(comparator_10_eq));  // open: gt, lt
  LookUpTable #(.Bits(9)) lookuptable_1 (
    .in0(R), .in1(I), .in2(IL), .in3(S), .in4(B), .in5(IS), .in6(J), .in7(U),
    .out({lookuptable_1_out[8], ImmSrc, ALUASrc, ALUBSrc, DMWr, RUDataWrSrc}));
  and and_2 (Br1, comparator_5_eq, B);
  and and_3 (Br2, comparator_6_eq, B);
  and and_4 (Br3, comparator_7_eq, B);
  and and_5 (Br4, comparator_8_eq, B);
  and and_6 (Br5, comparator_9_eq, B);
  and and_7 (Br6, comparator_10_eq, B);
  Multiplexer multiplexer_1 (.sel(Rd_t), .in_0(lookuptable_1_out[8]), .in_1(1'b0), .out(RUWr));
  LookUpTable #(.Bits(5)) BrTypeB (.in0(Br1), .in1(Br2), .in2(Br3), .in3(Br4), .in4(Br5), .in5(Br6), .out(BrB));
  Comparator #(.Bits(3)) u_DMCtrl (.a(Funct3), .b(3'b000), .eq(DMCtrl_eq));  // open: gt, lt
  Comparator #(.Bits(3)) comparator_11 (.a(Funct3), .b(3'b001), .eq(comparator_11_eq));  // open: gt, lt
  Comparator #(.Bits(3)) comparator_12 (.a(Funct3), .b(3'b010), .eq(comparator_12_eq));  // open: gt, lt
  Comparator #(.Bits(3)) comparator_13 (.a(Funct3), .b(3'b100), .eq(comparator_13_eq));  // open: gt, lt
  Comparator #(.Bits(3)) comparator_14 (.a(Funct3), .b(3'b101), .eq(comparator_14_eq));  // open: gt, lt
  LookUpTable #(.Bits(5)) Branch (.in0(R), .in1(I), .in2(IL), .in3(S), .in4(IS), .in5(J), .in6(U), .out(Br));
  and and_8 (and_8_out, DMCtrl_eq, IL);
  and and_9 (and_9_out, comparator_11_eq, IL);
  and and_10 (and_10_out, comparator_12_eq, IL);
  and and_11 (and_11_out, comparator_13_eq, IL);
  and and_12 (and_12_out, comparator_14_eq, IL);
  Multiplexer #(.Bits(5)) multiplexer_2 (.sel(B), .in_0(Br), .in_1(BrB), .out(BrOp));
  LookUpTable #(.Bits(3)) lookuptable_2 (
    .in0(and_8_out), .in1(and_9_out), .in2(and_10_out), .in3(and_11_out), .in4(and_12_out), .out(F3A));
  LookUpTable #(.Bits(3)) DMCtrl_2 (.in0(R), .in1(I), .in2(B), .in3(IS), .in4(J), .in5(U), .out(DM));
  Multiplexer #(.Selector_Bits(2), .Bits(3)) multiplexer_3 (
    .sel({S, IL}), .in_0(DM), .in_1(F3A), .in_2(F3B), .in_3(3'b000), .out(DMCtrl));
  and and_13 (addO, add, F7A);
  and and_14 (subO, sub, F7B);
  and and_15 (mulO, mul, F7C);
  and and_16 (srlO, srl, F7A);
  and and_17 (sraO, sra, F7B);
  and and_18 (srliO, srli, F7A);
  and and_19 (sraiO, srai, F7B);
  Comparator #(.Bits(3)) u_ADDI (.a(Funct3), .b(3'b000), .eq(addi));  // open: gt, lt
  Comparator #(.Bits(3)) u_SLLI (.a(Funct3), .b(3'b001), .eq(slli));  // open: gt, lt
  Comparator #(.Bits(3)) u_SLTI (.a(Funct3), .b(3'b010), .eq(slti));  // open: gt, lt
  Comparator #(.Bits(3)) u_SLTIU (.a(Funct3), .b(3'b011), .eq(sltiu));  // open: gt, lt
  Comparator #(.Bits(3)) u_XORI (.a(Funct3), .b(3'b100), .eq(xori));  // open: gt, lt
  Comparator #(.Bits(3)) u_SRLI (.a(Funct3), .b(3'b101), .eq(srli));  // open: gt, lt
  Comparator #(.Bits(3)) u_SRAI (.a(Funct3), .b(3'b101), .eq(srai));  // open: gt, lt
  Comparator #(.Bits(3)) u_ORI (.a(Funct3), .b(3'b110), .eq(ori));  // open: gt, lt
  Comparator #(.Bits(3)) u_ANDI (.a(Funct3), .b(3'b111), .eq(andi));  // open: gt, lt
  Comparator #(.Bits(3)) u_MUL (.a(Funct3), .b(3'b000), .eq(mul));  // open: gt, lt
  Comparator #(.Bits(3)) DMCtrl_3 (.a(Funct3), .b(3'b000), .eq(DMCtrl_3_eq));  // open: gt, lt
  Comparator #(.Bits(3)) comparator_15 (.a(Funct3), .b(3'b001), .eq(comparator_15_eq));  // open: gt, lt
  Comparator #(.Bits(3)) comparator_16 (.a(Funct3), .b(3'b010), .eq(comparator_16_eq));  // open: gt, lt
  or or_2 (or_2_out, IL, S, B, IS, J);
  and and_20 (and_20_out, DMCtrl_3_eq, S);
  and and_21 (and_21_out, comparator_15_eq, S);
  and and_22 (and_22_out, comparator_16_eq, S);
  LookUpTable #(.Bits(4)) Tipo_R_2 (
    .in0(addO), .in1(subO), .in2(sll), .in3(slt), .in4(sltu), .in5(\xor ), .in6(srlO), .in7(sraO),
    .in8(\or ), .in9(\and ), .in10(mul), .out(Rop));
  LookUpTable #(.Bits(4)) Tipo_I_2 (
    .in0(addi), .in1(slli), .in2(slti), .in3(sltiu), .in4(xori), .in5(srliO), .in6(sraiO), .in7(ori),
    .in8(andi), .out(Iop));
  LookUpTable #(.Bits(4)) lookuptable_3 (.in0(U), .in1(or_2_out), .out(Uop));
  LookUpTable #(.Bits(3)) lookuptable_4 (.in0(and_20_out), .in1(and_21_out), .in2(and_22_out), .out(F3B));
  Multiplexer #(.Selector_Bits(2), .Bits(4)) multiplexer_4 (
    .sel({R, I}), .in_0(Uop), .in_1(Iop), .in_2(Rop), .in_3(4'b0000), .out(ALUOp));

  // Other names for the same wires on the sheet: F3[2:0] = Funct3; F7[6:0] = Funct7

  // Notes on the sheet:
  //   Opcode: Define el tipo de instrucción a procesar
  //   Funct3: Define el tipo de operación y también el tipo de branch y DMCtrl
  //   Funct7: Diferencia entre add y sub, y entre sra y srl
  //   contents of lookuptable_1 (hex, n*v repeats v):
  //   0,1e0,108,0,109,0,0,0,2f,7*0,bb,15*0,10a,31*0,1da,63*0,48,71*0,1
  //   contents of BrTypeB (hex, n*v repeats v):
  //   0,8,a,0,b,0,0,0,8,7*0,d,15*0,e
  //   contents of Branch (hex, n*v repeats v):
  //   0,7,7,0,7,0,0,0,7,7*0,7,15*0,2710,31*0,7
  //   contents of lookuptable_2 (hex, n*v repeats v):
  //   0,6,5,0,4,0,0,0,2,7*0,1
  //   contents of DMCtrl_2 (hex, n*v repeats v):
  //   0,7,7,0,7,0,0,0,7,7*0,7,15*0,7
  //   contents of Tipo_R_2 (hex, n*v repeats v):
  //   0,0,8,0,1,0,0,0,2,7*0,3,15*0,4,31*0,5,63*0,d,127*0,6,255*0,7,511*0,e
  //   contents of Tipo_I_2 (hex, n*v repeats v):
  //   0,0,1,0,2,0,0,0,3,7*0,4,15*0,5,31*0,d,63*0,6,127*0,7
  //   contents of lookuptable_3 (hex, n*v repeats v):
  //   0,7
  //   contents of lookuptable_4 (hex, n*v repeats v):
  //   0,6,5,0,4
endmodule
