// Digital circuit DataMemory.dig as structural Verilog
module DataMemory (
  input  [2:0] DMCtrl,
  input  [31:0] DataWr,
  input  [31:0] Address,
  input  DMWr,
  input  Clk,
  output [31:0] DataRd
);

  // RAM32Bit #(.generic("addrBits :=24;")) ram32bit_1: pin names not known; wires that end beside it: Address, DataWr, DMWr, DMCtrl[1:0], DMCtrl[2], Clk, DataRd
endmodule
