// Digital circuit inst-decoder-B.dig as structural Verilog
module inst_decoder_B (
  input  [31:0] Inst,
  output [31:0] b
);

  BitExtender #(.inputBits(1), .outputBits(19)) bitextender_1 (.in(Inst[31]), .out(b[31:13]));

  assign b[12:0] = {Inst[31], Inst[7], Inst[30:25], Inst[11:8], 1'b0};
endmodule
