// Digital circuit inst-decoder-I.dig as structural Verilog
module inst_decoder_I (
  input  [31:0] Inst,
  output [31:0] Imm,
  output [31:0] shamt,
  output srai_srli
);

  BitExtender #(.inputBits(1), .outputBits(20)) bitextender_1 (.in(Inst[31]), .out(Imm[31:12]));

  assign Imm[11:0] = Inst[31:20];
  assign shamt = {{27{1'b0}}, Inst[24:20]};
  assign srai_srli = Inst[30];
endmodule
