// Digital circuit inst-decoder-J.dig as structural Verilog
module inst_decoder_J (
  input  [31:0] Inst,
  output [31:0] Imm
);

  BitExtender #(.inputBits(1), .outputBits(11)) bitextender_1 (.in(Inst[31]), .out(Imm[31:21]));

  assign Imm[20:0] = {Inst[31], Inst[19:12], Inst[20], Inst[30:21], 1'b0};
endmodule
