// Digital circuit inst-decoder-S.dig as structural Verilog
module inst_decoder_S (
  input  [31:0] Inst,
  output [31:0] Imm
);

  BitExtender #(.inputBits(1), .outputBits(20)) bitextender_1 (.in(Inst[31]), .out(Imm[31:12]));

  assign Imm[11:0] = {Inst[31:25], Inst[11:7]};
endmodule
