// Digital circuit instcase.dig as structural Verilog
module instcase (
  input  [31:0] Inst,
  output TypeR,
  output TypeI,
  output TypeIE,
  output TypelLoad,
  output TypeS,
  output TypeB,
  output TypeJ,
  output TypelJAL,
  output TypeULUI,
  output TypeUAUIPC,
  output TypelShift
);

  wire comparator_11_eq, comparator_12_eq, or_1_out;

  Comparator #(.Bits(7)) comparator_1 (.a(7'b0110011), .b(Inst[6:0]), .eq(TypeR));  // open: gt, lt
  Comparator #(.Bits(7)) comparator_2 (.a(7'b0010011), .b(Inst[6:0]), .eq(TypeI));  // open: gt, lt
  Comparator #(.Bits(7)) comparator_3 (.a(7'b1110011), .b(Inst[6:0]), .eq(TypeIE));  // open: gt, lt
  Comparator #(.Bits(7)) comparator_4 (.a(7'b0000011), .b(Inst[6:0]), .eq(TypelLoad));  // open: gt, lt
  Comparator #(.Bits(7)) comparator_5 (.a(7'b0100011), .b(Inst[6:0]), .eq(TypeS));  // open: gt, lt
  Comparator #(.Bits(7)) comparator_6 (.a(7'b1100011), .b(Inst[6:0]), .eq(TypeB));  // open: gt, lt
  Comparator #(.Bits(7)) comparator_7 (.a(7'b1101111), .b(Inst[6:0]), .eq(TypeJ));  // open: gt, lt
  Comparator #(.Bits(7)) comparator_8 (.a(7'b1100111), .b(Inst[6:0]), .eq(TypelJAL));  // open: gt, lt
  Comparator #(.Bits(7)) comparator_9 (.a(7'b0110111), .b(Inst[6:0]), .eq(TypeULUI));  // open: gt, lt
  Comparator #(.Bits(7)) comparator_10 (.a(7'b0010111), .b(Inst[6:0]), .eq(TypeUAUIPC));  // open: gt, lt
  Comparator #(.Bits(3)) comparator_11 (.a(Inst[14:12]), .b(3'b101), .eq(comparator_11_eq));  // open: gt, lt
  Comparator #(.Bits(7)) comparator_12 (.a(Inst[31:25]), .b(7'b0000001), .eq(comparator_12_eq));  // open: gt, lt
  or or_1 (or_1_out, comparator_11_eq, comparator_12_eq);
  and and_1 (TypelShift, TypeI, or_1_out);

  // Other names for the same wires on the sheet: F3[2:0] = Inst[14:12]; F7[6:0] = Inst[31:25]
endmodule
