// Digital circuit Immediate_generator.dig as structural Verilog
module Immediate_generator (
  input  [31:0] Inst,
  output [31:0] imm
);

  wire and_1_out, comparator_1_eq, comparator_2_eq, comparator_3_eq, comparator_4_eq, comparator_5_eq,
       comparator_6_eq, comparator_7_eq, comparator_8_eq, comparator_9_eq, comparator_10_eq,
       comparator_11_eq, or_1_out, or_2_out, or_3_out;
  wire [31:0] immb, immi, immj, imms, immu, multiplexer_1_out, multiplexer_2_out, multiplexer_3_out,
       multiplexer_4_out, multiplexer_5_out;

  BitExtender #(.inputBits(12), .outputBits(32)) bitextender_1 (.in(Inst[31:20]), .out(immi));
  BitExtender #(.inputBits(12), .outputBits(32)) bitextender_2 (.in({Inst[31:25], Inst[11:7]}), .out(imms));
  BitExtender #(.inputBits(13), .outputBits(32)) bitextender_3 (
    .in({Inst[31], Inst[7], Inst[30:25], Inst[11:8], 1'b0}), .out(immb));
  BitExtender #(.inputBits(20), .outputBits(32)) bitextender_4 (.in(Inst[31:12]), .out(immu));
  BitExtender #(.inputBits(21), .outputBits(32)) bitextender_5 (
    .in({Inst[31], Inst[19:12], Inst[20], Inst[30:21], 1'b0}), .out(immj));
  Comparator #(.Bits(7)) comparator_1 (.a(Inst[6:0]), .b(7'b0010011), .eq(comparator_1_eq));  // open: gt, lt
  Comparator #(.Bits(7)) comparator_2 (.a(Inst[6:0]), .b(7'b0000011), .eq(comparator_2_eq));  // open: gt, lt
  Comparator #(.Bits(7)) comparator_3 (.a(Inst[6:0]), .b(7'b1110011), .eq(comparator_3_eq));  // open: gt, lt
  Comparator #(.Bits(7)) comparator_4 (.a(Inst[6:0]), .b(7'b1100111), .eq(comparator_4_eq));  // open: gt, lt
  Comparator #(.Bits(3)) comparator_5 (.a(Inst[14:12]), .b(3'b101), .eq(comparator_5_eq));  // open: gt, lt
  Comparator #(.Bits(3)) comparator_6 (.a(Inst[14:12]), .b(3'b001), .eq(comparator_6_eq));  // open: gt, lt
  // Probe on {{27{1'b0}}, Inst[24:20]}
  // Probe on immu
  or or_1 (or_1_out, comparator_5_eq, comparator_6_eq);
  or or_2 (or_2_out, comparator_1_eq, comparator_2_eq, comparator_3_eq, comparator_4_eq);
  Comparator #(.Bits(7)) comparator_7 (.a(Inst[6:0]), .b(7'b0100011), .eq(comparator_7_eq));  // open: gt, lt
  Multiplexer #(.Bits(32)) multiplexer_1 (.sel(or_2_out), .in_0({32{1'b0}}), .in_1(immi), .out(multiplexer_1_out));
  and and_1 (and_1_out, comparator_1_eq, or_1_out);
  Comparator #(.Bits(7)) comparator_8 (.a(Inst[6:0]), .b(7'b1100011), .eq(comparator_8_eq));  // open: gt, lt
  Multiplexer #(.Bits(32)) multiplexer_2 (
    .sel(and_1_out), .in_0(multiplexer_1_out), .in_1({{27{1'b0}}, Inst[24:20]}), .out(multiplexer_2_out));
  Comparator #(.Bits(7)) comparator_9 (.a(Inst[6:0]), .b(7'b1101111), .eq(comparator_9_eq));  // open: gt, lt
  Comparator #(.Bits(7)) comparator_10 (.a(Inst[6:0]), .b(7'b0110111), .eq(comparator_10_eq));  // open: gt, lt
  Comparator #(.Bits(7)) comparator_11 (.a(Inst[6:0]), .b(7'b0010111), .eq(comparator_11_eq));  // open: gt, lt
  Multiplexer #(.Bits(32)) multiplexer_3 (
    .sel(comparator_7_eq), .in_0(multiplexer_2_out), .in_1(imms), .out(multiplexer_3_out));
  or or_3 (or_3_out, comparator_10_eq, comparator_11_eq);
  Multiplexer #(.Bits(32)) multiplexer_4 (
    .sel(comparator_8_eq), .in_0(multiplexer_3_out), .in_1(immb), .out(multiplexer_4_out));
  Multiplexer #(.Bits(32)) multiplexer_5 (
    .sel(comparator_9_eq), .in_0(multiplexer_4_out), .in_1(immj), .out(multiplexer_5_out));
  Multiplexer #(.Bits(32)) multiplexer_6 (.sel(or_3_out), .in_0(multiplexer_5_out), .in_1(immu), .out(imm));
  // Probe on imm
  // Probe on imm

  // Other names for the same wires on the sheet: opcode[6:0] = Inst[6:0]; func3[2:0] = Inst[14:12];
  //   shamt[4:0] = Inst[24:20]
endmodule
