// Digital circuit Instruction-Memory.dig as structural Verilog
module Instruction_Memory (
  input  [4:0] Addr,
  output [31:0] Inst
);

  EEPROM #(.AddrBits(5), .isProgramMemory("true"), .Bits(32)) eeprom_1 (
    .A(Addr), .CS(1'b1), .WE(1'b0), .OE(1'b1), .D(Inst));

  // Notes on the sheet:
  //   Addr: Direccion
  //   contents of eeprom_1 (hex, n*v repeats v):
  //   7302b3,40a48433,d615b3,107a733,13938b3,16aca33,19c5bb3,41cddd33
  //   ,3160b3,62f233,a30293,341393,f52493,1463593,574693,285793,40195893
  //   ,ca6993,7b7a93
endmodule
