// Digital circuit Instruction_memory.dig as structural Verilog
module Instruction_memory (
  input  [31:0] addr,
  output [31:0] inst
);

  wire [23:0] S2_s, S3_s, S4_s;

  ROM #(.AddrBits(24), .isProgramMemory("true"), .Bits(8)) ROM_1 (.A(addr[23:0]), .sel(1'b1), .D(inst[31:24]));
  Add #(.Bits(24)) S2 (.a(addr[23:0]), .b(24'h1), .c_i(1'b0), .s(S2_s));  // open: c_o
  Add #(.Bits(24)) S3 (.a(S2_s), .b(24'h1), .c_i(1'b0), .s(S3_s));  // open: c_o
  ROM #(.AddrBits(24), .Bits(8)) ROM_2 (.A(S2_s), .sel(1'b1), .D(inst[23:16]));
  Add #(.Bits(24)) S4 (.a(S3_s), .b(24'h1), .c_i(1'b0), .s(S4_s));  // open: c_o
  ROM #(.AddrBits(24), .Bits(8)) ROM_3 (.A(S3_s), .sel(1'b1), .D(inst[15:8]));
  ROM #(.AddrBits(24), .Bits(8)) ROM_4 (.A(S4_s), .sel(1'b1), .D(inst[7:0]));

  // Notes on the sheet:
  //   contents of ROM_1 (hex, n*v repeats v):
  //   12*0,2,0,0,0,ff,0,0,0,ff
  //   contents of ROM_2 (hex, n*v repeats v):
  //   0,50,0,0,0,10,0,0,0,5,0,0,0,a5,0,0,0,f5,0,0,0,5f,0,0,0,5
  //   contents of ROM_3 (hex, n*v repeats v):
  //   0,0,5,0,0,0,5,0,0,0,8,0,0,0,85,0,0,0,5,0,0,0,f0,0,0,0,85
  //   contents of ROM_4 (hex, n*v repeats v):
  //   0,0,0,13,0,0,0,93,0,0,0,63,0,0,0,b3,0,0,0,13,0,0,0,6f,0,0,0,93
endmodule
