// Digital circuit PC.dig as structural Verilog
module PC (
  input  reset,
  input  wen,
  input  clock,
  output [4:0] Output,
  output [4:0] ovf
);

  Counter #(.Bits(5)) counter_1 (.en(wen), .C(clock), .clr(reset), .out(Output), .ovf(ovf[0]));
  // Pins of 1 and 5 bits meet at ovf

  // Notes on the sheet:
  //   Output: El contador de programa actual
  //   reset: Provoca un salto absoluto. El valor de la entrada de la ALU se utiliza como la nueva dirección
  //   wen: Se activa si hay un salto relativo. El valor de la entrada de la ALU se le suma a la dirección actual
  //   ovf: El contador de programa actual
endmodule
