// Digital circuit Procesador Monociclo.dig as structural Verilog
module Procesador_Monociclo (
  input  in_3,
  output [31:0] out_1,
  output [31:0] out_2,
  output [31:0] out_4,
  output [2:0] out_5,
  output out_6,
  output out_7,
  output [31:0] out_8,
  output [1:0] out_9,
  output out_10,
  output [2:0] out_11,
  output out_12,
  output [31:0] out_13,
  output [6:0] out_14,
  output [4:0] out_15,
  output [31:0] out_16,
  output [31:0] out_17,
  output [3:0] out_18,
  output [2:0] out_19,
  output [4:0] out_20,
  output [4:0] out_21
);

  wire branchunit_1_nextpcsrc, clock, overflow;
  wire [4:0] controlunit_1_brop;
  wire [6:0] instruction_decoder_1_p2;
  wire [31:0] Address, dw, multiplexer_1_out, multiplexer_2_out, multiplexer_3_out, r10;

  Button button_1 (.out(clock));
  PC pc_1 (.Clk(clock), .InPC(multiplexer_3_out), .Reset(in_3), .OutPc(out_17));
  Add #(.Bits(32)) add_1 (.a(32'h4), .b(out_17), .c_i(1'b0), .s(Address), .c_o(overflow));
  Instruction_memory instruction_memory_1 (.addr(out_17[23:0]), .inst(out_4));
  // Instruction_Decoder instruction_decoder_1: pin names not known; wires that end beside it: out_4, instruction_decoder_1_p2, out_15, out_19, out_20, out_21, out_14
  ControlUnit controlunit_1 (
    .Opcode(instruction_decoder_1_p2), .Funct3(out_19), .Funct7(out_14), .Rd(out_15), .RUWr(out_12),
    .ImmSrc(out_11), .ALUASrc(out_6), .ALUBSrc(out_7), .DMWr(out_10), .BrOp(controlunit_1_brop),
    .DMCtrl(out_5), .ALUOp(out_18), .RUDataWrSrc(out_9));
  RegisterFile32Bits registerfile32bits_1 (
    .dataWrite(dw), .clock(clock), .rs1(out_20), .rs2(out_21), .rd(out_15), .EnableWrite(out_12),
    .rf_rs1(out_8), .rf_rs2(out_13), .r10(r10));
  Immediate_Generator immediate_generator_1 (
    .Inst_31_7({out_14, out_21, out_20, out_19, out_15}), .ImmSrc(out_11), .ImmExt(out_1));
  Multiplexer #(.Bits(32)) multiplexer_1 (.sel(out_6), .in_0(out_8), .in_1(out_17), .out(multiplexer_1_out));
  Multiplexer #(.Bits(32)) multiplexer_2 (.sel(out_7), .in_0(out_13), .in_1(out_1), .out(multiplexer_2_out));
  BranchUnit branchunit_1 (.RS1(out_8), .RS2(out_13), .BrOP(controlunit_1_brop), .NextPCSrc(branchunit_1_nextpcsrc));
  // ALU alu_1: pin names not known; wires that end beside it: out_18, multiplexer_1_out, multiplexer_2_out, out_16
  Multiplexer #(.Bits(32)) multiplexer_3 (
    .sel(branchunit_1_nextpcsrc), .in_0(Address), .in_1(out_16), .out(multiplexer_3_out));
  // DataMemory datamemory_1: pin names not known; wires that end beside it: out_5, out_13, out_16[23:0], out_10, clock, out_2
  Multiplexer #(.Selector_Bits(2), .Bits(32)) multiplexer_4 (
    .sel(out_9), .in_0(out_16), .in_1(out_2), .in_2(Address), .in_3({32{1'b0}}), .out(dw));

  // Other names for the same wires on the sheet: ALUASrc = out_6; ALUBSrc = out_7; ALUop[3:0] = out_18;
  //   ALUout[31:0] = out_16; dmCtrl[2:0] = out_5; dmOut[31:0] = out_2; dmWr = out_10; func3[2:0] = out_19;
  //   func7[6:0] = out_14; immOut[31:0] = out_1; immSrc[2:0] = out_11; outIm[31:0] = out_4; outPc[31:0] = out_17;
  //   rd[4:0] = out_15; reset = in_3; rf_rs1[31:0] = out_8; rf_rs2[31:0] = out_13; rfDataWrSrc[1:0] = out_9;
  //   rfWr = out_12; rs1[4:0] = out_20; rs2[4:0] = out_21

  // Notes on the sheet:
  //   fetch
  //   decode
  //   execute
  //   memory
  //   write back
endmodule
