// Digital circuit Procesador-Monociclo-RISCV_32Bits.dig as structural Verilog
module Procesador_Monociclo_RISCV_32Bits (
  input  CLOCK,
  input  RESET,
  input  ENABLE,
  input  [2:0] in_6,
  output [31:0] out_3,
  output [4:0] out_5
);

  wire [4:0] instruction_decoder_1_rd, instruction_decoder_1_rs1, instruction_decoder_1_rs2, pc_1_output;
  wire [31:0] instruction_memory_1_inst, registerfile_1_rs1data, registerfile_1_rs2data;

  PC pc_1 (.reset(RESET), .wen(ENABLE), .clock(CLOCK), .Output(pc_1_output), .ovf(out_5));
  Instruction_Memory instruction_memory_1 (.Addr(pc_1_output), .Inst(instruction_memory_1_inst));
  Instruction_Decoder instruction_decoder_1 (
    .Rd(instruction_decoder_1_rd), .Funct3(in_6), .Rs1(instruction_decoder_1_rs1),
    .Rs2(instruction_decoder_1_rs2), .Inst(instruction_memory_1_inst));  // open: Opcode
  control_unit control_unit_1 ();  // open: Inst, Imm_reg, rfwenable, dmwenable, brinst, jal_jalr, WBsel
  RegisterFile registerfile_1 (
    .enable(ENABLE), .rdAdrs(instruction_decoder_1_rd), .rdData(out_3), .rs1Adrs(instruction_decoder_1_rs1),
    .rs2Adrs(instruction_decoder_1_rs2), .clock(CLOCK), .rs1Data(registerfile_1_rs1data),
    .rs2Data(registerfile_1_rs2data));
  Immediate_generator immediate_generator_1 ();  // open: Inst, imm
  bjunit bjunit_1 ();  // open: rs1data, rs2data, binst, func3, jal, pcjump, rs1pc
  ALU_nBits alu_nbits_1 (.f3(in_6), .op_1(registerfile_1_rs1data), .op_2(registerfile_1_rs2data), .out(out_3));
  // Pins of 1 and 5 bits meet at out_5

  // Notes on the sheet:
  //   Procesador Monociclo RISC-V 32 BITS | Simple
endmodule
