// Digital circuit RegisterFile32Bits.dig as structural Verilog
module RegisterFile32Bits (
  input  [31:0] dataWrite,
  input  clock,
  input  [4:0] rs1,
  input  [4:0] rs2,
  input  [4:0] rd,
  input  EnableWrite,
  output [31:0] rf_rs1,
  output [31:0] rf_rs2,
  output [31:0] r10
);

  wire _3, _4, _5, _6, _7, _8, _9, _10, _11, _12, _13, _14, _15, _16, _17, _18, _19, _20, _21, _22, _23, _24,
       _25, _26, _27, _28, _29, _30, _31, _32, and_1_out, and_2_out, and_3_out, and_4_out, and_5_out,
       and_6_out, and_7_out, and_8_out, and_9_out, and_10_out, and_11_out, and_12_out, and_13_out,
       and_14_out, and_15_out, and_16_out, and_17_out, and_18_out, and_19_out, and_20_out, and_21_out,
       and_22_out, and_23_out, and_24_out, and_25_out, and_26_out, and_27_out, and_28_out, and_29_out,
       and_30_out, and_31_out, and_32_out, decoder_1_out_0, decoder_1_out_1;
  wire [31:0] s1, s2, s3, s4, s5, s6, s7, s8, s9, s10, s12, s13, s14, s15, s16, s17, s18, s19, s20, s21, s22,
       s23, s24, s25, s26, s27, s28, s29, s30, s31, s32;

  Decoder #(.Selector_Bits(5)) decoder_1 (
    .sel(rd), .out_0(decoder_1_out_0), .out_1(decoder_1_out_1), .out_2(_3), .out_3(_4), .out_4(_5),
    .out_5(_6), .out_6(_7), .out_7(_8), .out_8(_9), .out_9(_10), .out_10(_11), .out_11(_12), .out_12(_13),
    .out_13(_14), .out_14(_15), .out_15(_16), .out_16(_17), .out_17(_18), .out_18(_19), .out_19(_20),
    .out_20(_21), .out_21(_22), .out_22(_23), .out_23(_24), .out_24(_25), .out_25(_26), .out_26(_27),
    .out_27(_28), .out_28(_29), .out_29(_30), .out_30(_31), .out_31(_32));
  and and_1 (and_1_out, decoder_1_out_0, EnableWrite);
  and and_2 (and_2_out, decoder_1_out_1, EnableWrite);
  and and_3 (and_3_out, _3, EnableWrite);
  and and_4 (and_4_out, _4, EnableWrite);
  and and_5 (and_5_out, _5, EnableWrite);
  and and_6 (and_6_out, _6, EnableWrite);
  and and_7 (and_7_out, _7, EnableWrite);
  and and_8 (and_8_out, _8, EnableWrite);
  and and_9 (and_9_out, _9, EnableWrite);
  and and_10 (and_10_out, _10, EnableWrite);
  and and_11 (and_11_out, _11, EnableWrite);
  and and_12 (and_12_out, _12, EnableWrite);
  and and_13 (and_13_out, _13, EnableWrite);
  and and_14 (and_14_out, _14, EnableWrite);
  and and_15 (and_15_out, _15, EnableWrite);
  and and_16 (and_16_out, _16, EnableWrite);
  and and_17 (and_17_out, _17, EnableWrite);
  and and_18 (and_18_out, _18, EnableWrite);
  and and_19 (and_19_out, _19, EnableWrite);
  and and_20 (and_20_out, _20, EnableWrite);
  and and_21 (and_21_out, _21, EnableWrite);
  and and_22 (and_22_out, _22, EnableWrite);
  and and_23 (and_23_out, _23, EnableWrite);
  and and_24 (and_24_out, _24, EnableWrite);
  and and_25 (and_25_out, _25, EnableWrite);
  and and_26 (and_26_out, _26, EnableWrite);
  and and_27 (and_27_out, _27, EnableWrite);
  and and_28 (and_28_out, _28, EnableWrite);
  and and_29 (and_29_out, _29, EnableWrite);
  and and_30 (and_30_out, _30, EnableWrite);
  and and_31 (and_31_out, _31, EnableWrite);
  and and_32 (and_32_out, _32, EnableWrite);
  Register #(.Bits(32)) register_1 (.D(dataWrite), .C(clock), .en(and_1_out), .Q(s1));
  Register #(.Bits(32)) register_2 (.D(dataWrite), .C(clock), .en(and_2_out), .Q(s2));
  Register #(.Bits(32)) register_3 (.D(dataWrite), .C(clock), .en(and_3_out), .Q(s3));
  Register #(.Bits(32)) register_4 (.D(dataWrite), .C(clock), .en(and_4_out), .Q(s4));
  Register #(.Bits(32)) register_5 (.D(dataWrite), .C(clock), .en(and_5_out), .Q(s5));
  Register #(.Bits(32)) register_6 (.D(dataWrite), .C(clock), .en(and_6_out), .Q(s6));
  Register #(.Bits(32)) register_7 (.D(dataWrite), .C(clock), .en(and_7_out), .Q(s7));
  Register #(.Bits(32)) register_8 (.D(dataWrite), .C(clock), .en(and_8_out), .Q(s8));
  Register #(.Bits(32)) register_9 (.D(dataWrite), .C(clock), .en(and_9_out), .Q(s9));
  Register #(.Bits(32)) register_10 (.D(dataWrite), .C(clock), .en(and_10_out), .Q(s10));
  Register #(.Bits(32)) register_11 (.D(dataWrite), .C(clock), .en(and_11_out), .Q(r10));
  Register #(.Bits(32)) register_12 (.D(dataWrite), .C(clock), .en(and_12_out), .Q(s12));
  Register #(.Bits(32)) register_13 (.D(dataWrite), .C(clock), .en(and_13_out), .Q(s13));
  Register #(.Bits(32)) register_14 (.D(dataWrite), .C(clock), .en(and_14_out), .Q(s14));
  Register #(.Bits(32)) register_15 (.D(dataWrite), .C(clock), .en(and_15_out), .Q(s15));
  Register #(.Bits(32)) register_16 (.D(dataWrite), .C(clock), .en(and_16_out), .Q(s16));
  Register #(.Bits(32)) register_17 (.D(dataWrite), .C(clock), .en(and_17_out), .Q(s17));
  Register #(.Bits(32)) register_18 (.D(dataWrite), .C(clock), .en(and_18_out), .Q(s18));
  Register #(.Bits(32)) register_19 (.D(dataWrite), .C(clock), .en(and_19_out), .Q(s19));
  Register #(.Bits(32)) register_20 (.D(dataWrite), .C(clock), .en(and_20_out), .Q(s20));
  Register #(.Bits(32)) register_21 (.D(dataWrite), .C(clock), .en(and_21_out), .Q(s21));
  Register #(.Bits(32)) register_22 (.D(dataWrite), .C(clock), .en(and_22_out), .Q(s22));
  Register #(.Bits(32)) register_23 (.D(dataWrite), .C(clock), .en(and_23_out), .Q(s23));
  Register #(.Bits(32)) register_24 (.D(dataWrite), .C(clock), .en(and_24_out), .Q(s24));
  Register #(.Bits(32)) register_25 (.D(dataWrite), .C(clock), .en(and_25_out), .Q(s25));
  Register #(.Bits(32)) register_26 (.D(dataWrite), .C(clock), .en(and_26_out), .Q(s26));
  Register #(.Bits(32)) register_27 (.D(dataWrite), .C(clock), .en(and_27_out), .Q(s27));
  Register #(.Bits(32)) register_28 (.D(dataWrite), .C(clock), .en(and_28_out), .Q(s28));
  Register #(.Bits(32)) register_29 (.D(dataWrite), .C(clock), .en(and_29_out), .Q(s29));
  Register #(.Bits(32)) register_30 (.D(dataWrite), .C(clock), .en(and_30_out), .Q(s30));
  Register #(.Bits(32)) register_31 (.D(dataWrite), .C(clock), .en(and_31_out), .Q(s31));
  Register #(.Bits(32)) register_32 (.D(dataWrite), .C(clock), .en(and_32_out), .Q(s32));
  Multiplexer #(.Selector_Bits(5), .Bits(32)) multiplexer_1 (
    .sel(rs1), .in_0(s1), .in_1(s2), .in_2(s3), .in_3(s4), .in_4(s5), .in_5(s6), .in_6(s7), .in_7(s8),
    .in_8(s9), .in_9(s10), .in_10(r10), .in_11(s12), .in_12(s13), .in_13(s14), .in_14(s15), .in_15(s16),
    .in_16(s17), .in_17(s18), .in_18(s19), .in_19(s20), .in_20(s21), .in_21(s22), .in_22(s23), .in_23(s24),
    .in_24(s25), .in_25(s26), .in_26(s27), .in_27(s28), .in_28(s29), .in_29(s30), .in_30(s31), .in_31(s32),
    .out(rf_rs1));
  Multiplexer #(.Selector_Bits(5), .Bits(32)) multiplexer_2 (
    .sel(rs2), .in_0(s1), .in_1(s2), .in_2(s3), .in_3(s4), .in_4(s5), .in_5(s6), .in_6(s7), .in_7(s8),
    .in_8(s9), .in_9(s10), .in_10(r10), .in_11(s12), .in_12(s13), .in_13(s14), .in_14(s15), .in_15(s16),
    .in_16(s17), .in_17(s18), .in_18(s19), .in_19(s20), .in_20(s21), .in_21(s22), .in_22(s23), .in_23(s24),
    .in_24(s25), .in_25(s26), .in_26(s27), .in_27(s28), .in_28(s29), .in_29(s30), .in_30(s31), .in_31(s32),
    .out(rf_rs2));

  // Other names for the same wires on the sheet: Control_1[4:0] = rs1; Control_2[4:0] = rs2; s11[31:0] = r10
endmodule
