// Digital circuit bjunit.dig as structural Verilog
module bjunit (
  input  [31:0] rs1data,
  input  [31:0] rs2data,
  input  binst,
  input  [2:0] func3,
  input  jal,
  output pcjump,
  output rs1pc
);

  wire eq__eq_eq, eq_eq, gt__eq__U_lt, gt__eq_lt, lt__U_lt, lt_lt, multiplexer_1_out, not_1_out, not_2_out;

  Comparator #(.Signed("true"), .Bits(32)) eq__eq (.a(rs1data), .b(rs2data), .eq(eq__eq_eq));  // open: gt, lt
  Comparator #(.Signed("true"), .Bits(32)) eq (.a(rs1data), .b(rs2data), .eq(eq_eq));  // open: gt, lt
  Comparator #(.Signed("true"), .Bits(32)) lt (.a(rs1data), .b(rs2data), .lt(lt_lt));  // open: gt, eq
  Comparator #(.Signed("true"), .Bits(32)) gt__eq (.a(rs1data), .b(rs2data), .lt(gt__eq_lt));  // open: gt, eq
  Comparator #(.Bits(32)) lt__U (.a(rs1data), .b(rs2data), .lt(lt__U_lt));  // open: gt, eq
  Comparator #(.Bits(32)) gt__eq__U (.a(rs2data), .b(rs1data), .lt(gt__eq__U_lt));  // open: gt, eq
  not not_1 (not_1_out, eq_eq);
  not not_2 (not_2_out, gt__eq_lt);
  Multiplexer #(.Selector_Bits(3)) multiplexer_1 (
    .sel(func3), .in_0(eq__eq_eq), .in_1(not_1_out), .in_2(1'b0), .in_3(1'b0), .in_4(lt_lt),
    .in_5(not_2_out), .in_6(lt__U_lt), .in_7(gt__eq__U_lt), .out(multiplexer_1_out));
  Multiplexer multiplexer_2 (.sel(binst), .in_0(jal), .in_1(multiplexer_1_out), .out(rs1pc));
  or or_1 (pcjump, rs1pc, jal);

  // Other names for the same wires on the sheet: jtype = jal; rs1[31:0] = rs1data; rs2[31:0] = rs2data
endmodule
