// Digital circuit control_unit.dig as structural Verilog
module control_unit (
  input  [31:0] Inst,
  output Imm_reg,
  output rfwenable,
  output dmwenable,
  output brinst,
  output jal_jalr,
  output [1:0] WBsel
);

  wire jal_eq, jalr_eq, type_R, useDM;
  wire [1:0] multiplexer_1_out;

  Comparator #(.Bits(7)) u_type_R (.a(Inst[6:0]), .b(7'b0110011), .eq(type_R));  // open: gt, lt
  Comparator #(.Bits(7)) type_S (.a(Inst[6:0]), .b(7'b0100011), .eq(dmwenable));  // open: gt, lt
  Comparator #(.Bits(7)) type_B (.a(Inst[6:0]), .b(7'b1100011), .eq(brinst));  // open: gt, lt
  Comparator #(.Bits(7)) jal (.a(Inst[6:0]), .b(7'b1101111), .eq(jal_eq));  // open: gt, lt
  Comparator #(.Bits(7)) jalr (.a(Inst[6:0]), .b(7'b1100111), .eq(jalr_eq));  // open: gt, lt
  Multiplexer #(.Bits(2)) multiplexer_1 (.sel(useDM), .in_0(2'b00), .in_1(2'b01), .out(multiplexer_1_out));
  Comparator #(.Bits(7)) load (.a(Inst[6:0]), .b(7'b0000011), .eq(useDM));  // open: gt, lt
  not not_1 (Imm_reg, type_R);
  nor nor_1 (rfwenable, dmwenable, brinst);
  or or_1 (jal_jalr, jal_eq, jalr_eq);
  Multiplexer #(.Bits(2)) multiplexer_2 (.sel(jal_jalr), .in_0(multiplexer_1_out), .in_1(2'b10), .out(WBsel));
endmodule
