// Digital circuit BranchUnit1.dig as structural Verilog
module BranchUnit1 (
  input  [31:0] RS1,
  input  [31:0] RS2,
  input  [4:0] BrOP,
  output NextPCSrc
);

  wire BEQ, BGE, BGE_eq, BGE_gt, BGEU, BGEU_eq, BGEU_gt, BLT, BLTU, BNE, BNE_eq;

  Comparator #(.Signed("true"), .Bits(32)) u_BEQ (.a(RS1), .b(RS2), .eq(BEQ));  // open: gt, lt
  Comparator #(.Signed("true"), .Bits(32)) u_BNE (.a(RS1), .b(RS2), .eq(BNE_eq));  // open: gt, lt
  Comparator #(.Signed("true"), .Bits(32)) u_BLT (.a(RS1), .b(RS2), .lt(BLT));  // open: gt, eq
  not not_1 (BNE, BNE_eq);
  Comparator #(.Signed("true"), .Bits(32)) u_BGE (.a(RS1), .b(RS2), .gt(BGE_gt), .eq(BGE_eq));  // open: lt
  Comparator #(.Bits(32)) u_BLTU (.a(RS1), .b(RS2), .lt(BLTU));  // open: gt, eq
  Comparator #(.Bits(32)) u_BGEU (.a(RS1), .b(RS2), .gt(BGEU_gt), .eq(BGEU_eq));  // open: lt
  or or_1 (BGE, BGE_gt, BGE_eq);
  or or_2 (BGEU, BGEU_gt, BGEU_eq);
  Multiplexer #(.Selector_Bits(5)) multiplexer_1 (
    .sel(BrOP), .in_0(1'b0), .in_1(1'b0), .in_2(1'b0), .in_3(1'b0), .in_4(1'b0), .in_5(1'b0), .in_6(1'b0),
    .in_7(1'b0), .in_8(BEQ), .in_9(1'b0), .in_10(BNE), .in_11(BLT), .in_12(1'b0), .in_13(BLTU), .in_14(BGEU),
    .in_15(BGE), .in_16(1'b1), .in_17(1'b1), .in_18(1'b1), .in_19(1'b1), .in_20(1'b1), .in_21(1'b1),
    .in_22(1'b1), .in_23(1'b1), .in_24(1'b1), .in_25(1'b1), .in_26(1'b1), .in_27(1'b1), .in_28(1'b1),
    .in_29(1'b1), .in_30(1'b1), .in_31(1'b1), .out(NextPCSrc));
endmodule
