// Digital circuit Display.dig as structural Verilog
module Display (
  input  [31:0] ALUOut,
  output [3:0] D1,
  output [3:0] D2,
  output [3:0] D3,
  output [3:0] D4,
  output [3:0] D5,
  output [3:0] D6,
  output [3:0] D7,
  output [3:0] D8
);


  assign D1 = ALUOut[3:0];
  assign D2 = ALUOut[7:4];
  assign D3 = ALUOut[11:8];
  assign D4 = ALUOut[15:12];
  assign D5 = ALUOut[19:16];
  assign D6 = ALUOut[23:20];
  assign D7 = ALUOut[27:24];
  assign D8 = ALUOut[31:28];
endmodule
