// Digital circuit Immediate Generator.dig as structural Verilog
module Immediate_Generator (
  input  [24:0] Inst_31_7,
  input  [2:0] ImmSrc,
  output [31:0] ImmExt
);

  wire [31:0] Bimm, Iimm, Jimm, Simm, Uimm;

  BitExtender #(.inputBits(12), .outputBits(32)) Type_I (.in(Inst_31_7[24:13]), .out(Iimm));
  BitExtender #(.inputBits(20), .outputBits(32)) Type_U (.in(Inst_31_7[24:5]), .out(Uimm));
  BitExtender #(.inputBits(12), .outputBits(32)) Type_S (.in({Inst_31_7[24:18], Inst_31_7[4:0]}), .out(Simm));
  BitExtender #(.inputBits(13), .outputBits(32)) Type_B (
    .in({Inst_31_7[24], Inst_31_7[0], Inst_31_7[23:18], Inst_31_7[4:1], 1'b0}), .out(Bimm));
  BitExtender #(.inputBits(21), .outputBits(32)) Type_J (
    .in({Inst_31_7[24], Inst_31_7[12:5], Inst_31_7[13], Inst_31_7[23:14], 1'b0}), .out(Jimm));
  Multiplexer #(.Selector_Bits(3), .Bits(32)) multiplexer_1 (
    .sel(ImmSrc), .in_0(Iimm), .in_1(Simm), .in_2(Uimm), .in_3({32{1'b0}}), .in_4({32{1'b0}}), .in_5(Bimm),
    .in_6(Jimm), .in_7({32{1'b0}}), .out(ImmExt));

  // Other names for the same wires on the sheet: Inst[24:0] = Inst_31_7

  // Notes on the sheet:
  //   Inst_31_7: 25 bits posibles de inmediato
  //   ImmSrc: Indica el tipo de instrucción
endmodule
