// Digital circuit Instruction Memory.dig as structural Verilog
module Instruction_Memory (
  input  [23:0] OutPc,
  output [31:0] Instruction
);

  EEPROM #(.AddrBits(24), .isProgramMemory("true"), .Bits(32)) eeprom_1 (
    .A(OutPc), .CS(1'b1), .WE(1'b0), .OE(1'b1), .D(Instruction));

  // Notes on the sheet:
  //   contents of eeprom_1 (hex, n*v repeats v):
  //   fe010113,0,0,0,112e23,0,0,0,812c23,0,0,0,2010413,0,0,0,a00793
  //   ,0,0,0,fef42623,0,0,0,fec42703,0,0,0,100793,0,0,0,e7c663,0,0,0
  //   ,100793,0,0,0,3c0006f,0,0,0,100793,0,0,0,fef42423,0,0,0,200006f
  //   ,0,0,0,fe842703,0,0,0,fec42783,0,0,0,2f707b3,0,0,0,fef42423,0,0,0
  //   ,fec42783,0,0,0,fff78793,0,0,0,fef42623,0,0,0,fec42703,0,0,0,100793
  //   ,0,0,0,fce7cee3,0,0,0,fe842783,0,0,0,78513,0,0,0,1c12083,0,0,0
  //   ,1812403,0,0,0,2010113,0,0,0,8067
endmodule
