// Digital circuit PC1.dig as structural Verilog
module PC1 (
  input  Clk,
  input  [31:0] InPC,
  input  Reset,
  output [31:0] OutPc
);

  wire [31:0] multiplexer_1_out;

  Multiplexer #(.Bits(32)) multiplexer_1 (.sel(Reset), .in_0(InPC), .in_1({32{1'b0}}), .out(multiplexer_1_out));
  Register #(.Bits(32)) register_1 (.D(multiplexer_1_out), .C(Clk), .en(1'b1), .Q(OutPc));
endmodule
