// Digital circuit Procesador Monociclo - Steven Grisales.dig as structural Verilog
module Procesador_Monociclo___Steven_Grisales (
  input  Clk,
  input  Reset,
  output [31:0] out_1,
  output [31:0] ImmExt,
  output [31:0] DMOut,
  output [31:0] out_4,
  output [31:0] out_5,
  output [31:0] out_6,
  output [31:0] out_7,
  output [3:0] out_8,
  output [2:0] out_9,
  output [1:0] out_10,
  output out_11,
  output out_12,
  output out_13,
  output [2:0] out_14,
  output out_15,
  output [2:0] Funct_3,
  output [6:0] Funct7,
  output [4:0] Rd
);

  wire branchunit_1_nextpcsrc, Overflow;
  wire [3:0] D1, D2, D3, D4, D5, D6, D7, D8;
  wire [4:0] controlunit_1_brop;
  wire [31:0] Address, Dw, multiplexer_1_out, multiplexer_2_out, multiplexer_3_out, r10;

  PC pc_1 (.Clk(Clk), .InPC(multiplexer_3_out), .Reset(Reset), .OutPc(out_4));
  Instruction_Memory instruction_memory_1 (
    .OutPc(out_4[23:0]), .Instruction({Funct7, out_5[24:15], Funct_3, out_5[11:0]}));
  Display display_1 (.ALUOut(out_1), .D1(D1), .D2(D2), .D3(D3), .D4(D4), .D5(D5), .D6(D6), .D7(D7), .D8(D8));
  Add #(.Bits(32)) add_1 (.a(32'h4), .b(out_4), .c_i(1'b0), .s(Address), .c_o(Overflow));
  Seven_Seg_Hex seven_seg_hex_1 (.d(r10[31:28]), .dp(1'b0));
  Seven_Seg_Hex seven_seg_hex_2 (.d(D8), .dp(1'b0));
  ControlUnit controlunit_1 (
    .Opcode(out_5[6:0]), .Funct3(Funct_3), .Funct7(Funct7), .Rd(out_5[11:7]), .RUWr(out_15), .ImmSrc(out_14),
    .ALUASrc(out_13), .ALUBSrc(out_12), .DMWr(out_11), .BrOp(controlunit_1_brop), .DMCtrl(out_9),
    .ALUOp(out_8), .RUDataWrSrc(out_10));
  Seven_Seg_Hex seven_seg_hex_3 (.d(r10[27:24]), .dp(1'b0));
  Seven_Seg_Hex seven_seg_hex_4 (.d(D7), .dp(1'b0));
  Immediate_Generator immediate_generator_1 (
    .Inst_31_7({Funct7, out_5[24:15], Funct_3, out_5[11:7]}), .ImmSrc(out_14), .ImmExt(ImmExt));
  Seven_Seg_Hex seven_seg_hex_5 (.d(r10[23:20]), .dp(1'b0));
  Seven_Seg_Hex seven_seg_hex_6 (.d(D6), .dp(1'b0));
  RegisterFile32Bits registerfile32bits_1 (
    .DataWrite(Dw), .Clock(Clk), .Rs1(out_5[19:15]), .Rs2(out_5[24:20]), .Rd(out_5[11:7]),
    .EnableWrite(out_15), .RU_rs1(out_6), .RU_rs2(out_7), .r10(r10));
  Seven_Seg_Hex seven_seg_hex_7 (.d(r10[15:12]), .dp(1'b0));
  Seven_Seg_Hex seven_seg_hex_8 (.d(r10[19:16]), .dp(1'b0));
  Seven_Seg_Hex seven_seg_hex_9 (.d(D5), .dp(1'b0));
  Seven_Seg_Hex seven_seg_hex_10 (.d(r10[11:8]), .dp(1'b0));
  Seven_Seg_Hex seven_seg_hex_11 (.d(D4), .dp(1'b0));
  Seven_Seg_Hex seven_seg_hex_12 (.d(r10[7:4]), .dp(1'b0));
  Seven_Seg_Hex seven_seg_hex_13 (.d(D3), .dp(1'b0));
  Seven_Seg_Hex seven_seg_hex_14 (.d(r10[3:0]), .dp(1'b0));
  Seven_Seg_Hex seven_seg_hex_15 (.d(D2), .dp(1'b0));
  Multiplexer #(.Bits(32)) multiplexer_1 (.sel(out_13), .in_0(out_6), .in_1(out_4), .out(multiplexer_1_out));
  Multiplexer #(.Bits(32)) multiplexer_2 (.sel(out_12), .in_0(out_7), .in_1(ImmExt), .out(multiplexer_2_out));
  Seven_Seg_Hex seven_seg_hex_16 (.d(D1), .dp(1'b0));
  BranchUnit branchunit_1 (.RS1(out_6), .RS2(out_7), .BrOP(controlunit_1_brop), .NextPCSrc(branchunit_1_nextpcsrc));
  ALU alu_1 (.ALUOp(out_8), .A(multiplexer_1_out), .B(multiplexer_2_out), .out(out_1));
  Multiplexer #(.Bits(32)) multiplexer_3 (
    .sel(branchunit_1_nextpcsrc), .in_0(Address), .in_1(out_1), .out(multiplexer_3_out));
  // DataMemory datamemory_1: pin names not known; wires that end beside it: out_9, out_7, out_1[23:0], out_11, Clk, DMOut
  Multiplexer #(.Selector_Bits(2), .Bits(32)) multiplexer_4 (
    .sel(out_10), .in_0(out_1), .in_1(DMOut), .in_2(Address), .in_3({32{1'b0}}), .out(Dw));

  assign {out_5[31:25], out_5[14:12]} = {Funct7, Funct_3};
  assign Rd = out_5[11:7];

  // Other names for the same wires on the sheet: ALUASrc = out_13; ALUBSrc = out_12; ALUOP[3:0] = out_8;
  //   ALUOut[31:0] = out_1; DMCtrl[2:0] = out_9; DMWr = out_11; ImmSrc[2:0] = out_14;
  //   IMOut[31:0] = {Funct7, out_5[24:15], Funct_3, out_5[11:0]}; Funct3[2:0] = Funct_3; RS1[4:0] = out_5[19:15];
  //   RS2[4:0] = out_5[24:20]; OutPC[31:0] = out_4; RU_rs1[31:0] = out_6; RU_rs2[31:0] = out_7;
  //   RUDataWrSrc[1:0] = out_10; RUWr = out_15

  // Notes on the sheet:
  //   Clk: Hz: 2147483647
  //   ALU OP:
  //   0000: A + B
  //   0001: A << B
  //   0010: A < B
  //   0011: A < B(U)
  //   0100: A XOR B
  //   0101 A >> B
  //   0110: A OR B
  //   0111: A AND B
  //   1000: A - B
  //   1101: A >>> B
  //   Resultado ALU
  //   Resultado Factorial (registro 10)
endmodule
