// Digital circuit Procesador Monociclo.dig as structural Verilog
module Procesador_Monociclo (
  input  Reset,
  output [31:0] immExt,
  output [31:0] DMOut,
  output [31:0] out_4,
  output [2:0] out_5,
  output out_6,
  output out_7,
  output [31:0] out_8,
  output [1:0] out_9,
  output out_10,
  output [2:0] out_11,
  output out_12,
  output [31:0] out_13,
  output [6:0] Funct7,
  output [4:0] Rd,
  output [31:0] out_16,
  output [31:0] out_17,
  output [3:0] out_18,
  output [2:0] Funct_3
);

  wire branchunit_1_nextpcsrc, clock, Overflow;
  wire [4:0] controlunit_1_brop, rs1, rs2;
  wire [6:0] instruction_decoder_1_p2;
  wire [31:0] Address, dw, multiplexer_1_out, multiplexer_2_out, multiplexer_3_out, r10;

  Button button_1 (.out(clock));
  PC pc_1 (.Clk(clock), .InPC(multiplexer_3_out), .Reset(Reset), .OutPc(out_17));
  Instruction_Memory instruction_memory_1 (.OutPc(out_17[23:0]), .Instruction(out_4));
  Add #(.Bits(32)) add_1 (.a(32'h4), .b(out_17), .c_i(1'b0), .s(Address), .c_o(Overflow));
  // Instruction_Decoder instruction_decoder_1: pin names not known; wires that end beside it: out_4, instruction_decoder_1_p2, Rd, Funct_3, rs1, rs2, Funct7
  ControlUnit controlunit_1 (
    .Opcode(instruction_decoder_1_p2), .Funct3(Funct_3), .Funct7(Funct7), .Rd(Rd), .RUWr(out_12),
    .ImmSrc(out_11), .ALUASrc(out_6), .ALUBSrc(out_7), .DMWr(out_10), .BrOp(controlunit_1_brop),
    .DMCtrl(out_5), .ALUOp(out_18), .RUDataWrSrc(out_9));
  RegisterFile32Bits registerfile32bits_1 (
    .DataWrite(dw), .Clock(clock), .Rs1(rs1), .Rs2(rs2), .Rd(Rd), .EnableWrite(out_12), .RU_rs1(out_8),
    .RU_rs2(out_13), .r10(r10));
  Immediate_Generator immediate_generator_1 (
    .Inst_31_7({Funct7, rs2, rs1, Funct_3, Rd}), .ImmSrc(out_11), .ImmExt(immExt));
  Multiplexer #(.Bits(32)) multiplexer_1 (.sel(out_6), .in_0(out_8), .in_1(out_17), .out(multiplexer_1_out));
  Multiplexer #(.Bits(32)) multiplexer_2 (.sel(out_7), .in_0(out_13), .in_1(immExt), .out(multiplexer_2_out));
  BranchUnit branchunit_1 (.RS1(out_8), .RS2(out_13), .BrOP(controlunit_1_brop), .NextPCSrc(branchunit_1_nextpcsrc));
  // ALU alu_1: pin names not known; wires that end beside it: out_18, multiplexer_1_out, multiplexer_2_out, out_16
  Multiplexer #(.Bits(32)) multiplexer_3 (
    .sel(branchunit_1_nextpcsrc), .in_0(Address), .in_1(out_16), .out(multiplexer_3_out));
  // DataMemory datamemory_1: pin names not known; wires that end beside it: out_5, out_13, out_16[23:0], out_10, clock, DMOut
  Multiplexer #(.Selector_Bits(2), .Bits(32)) multiplexer_4 (
    .sel(out_9), .in_0(out_16), .in_1(DMOut), .in_2(Address), .in_3({32{1'b0}}), .out(dw));

  // Other names for the same wires on the sheet: ALUASrc = out_6; ALUBSrc = out_7; ALUop[3:0] = out_18;
  //   ALUout[31:0] = out_16; dmCtrl[2:0] = out_5; DMWr = out_10; func3[2:0] = Funct_3; func7[6:0] = Funct7;
  //   immSrc[2:0] = out_11; outIm[31:0] = out_4; outPc[31:0] = out_17; ru_rs1[31:0] = out_8; ru_rs2[31:0] = out_13;
  //   RUDataWrSrc[1:0] = out_9; ruwR = out_12
endmodule
